# Fritzing sketch moteur (saved by Fritzing 0.9.3b)
breadboards: 1

parts:
  S1 = H-Bridge with L298N
  M1 = DC Motor
  M2 = DC Motor
  Part1 = Arduino Uno (Rev3) - ICSP
  VCC1 = 4 x AAA Battery Mount

nets:
  N1: S1.12V, VCC1.+
  GND: S1.GND, Part1.GND, VCC1.-
  N2: S1.ENA, S1.ENA-5V
  N3: S1.IN1, Part1.D5_PWM
  N4: S1.IN2, Part1.D6_PWM
  N5: S1.IN3, Part1.D9_PWM
  N6: S1.IN4, Part1.D10_PWM/SS
  N7: S1.ENB, S1.ENB-5V
  N8: S1.M1-01, M2.pin_2
  N9: S1.M1-02, M2.pin_1
  N10: S1.M2-01, M1.pin_2
  N11: S1.M2-02, M1.pin_1

custom parts:
  H-Bridge with L298N: h-bridge
